// Digital circuit CircuitDiagram.dig as structural Verilog
module CircuitDiagram (
);

  Add add_1 ();  // open: a, b, c_i, s, c_o
  Sub sub_1 ();  // open: a, b, c_i, s, c_o
  Mul mul_1 ();  // open: a, b, mul
  Div div_1 ();  // open: a, b, q, r
  // And and_1 is placed but not wired
  // Or or_1 is placed but not wired
  // Not not_1 is placed but not wired
  // XOr xor_1 is placed but not wired
  Decoder decoder_1 ();  // open: sel, out_0, out_1
  Multiplexer multiplexer_1 ();  // open: sel, in_0, in_1, out
  D_FF d_ff_1 ();  // open: D, C, Q, nQ

  // Notes on the sheet:
  //   16-bit Adder
  //   16-bit Subtractor
  //   (has overflow check)
  //   16-bit Multiplier
  //   (output can go up to 32-bits)
  //   16-bit Divider
  //   16-bit AND
  //   16-bit OR
  //   16-bit NOT
  //   16-bit XOR
  //   16x32-bit MUX
  //   (how to??)
  //   Decoder 
  //   (why does it look like that)
  //   32-bit accumulator
  //   (made up of 32 1-bit D Flip-Flops)
endmodule
